# Fritzing sketch IIe headphone jack (saved by Fritzing 0.9.2b)
circuit board: 1.9687cm x 1.56828cm
breadboards: 1

parts:
  TO_SPEAKER = female pin header, 2 pins [form="♀ (female)"]
  J19 = female alternating pin header, 1 pin [form="♀ (female)"]
  J20 = female alternating pin header, 1 pin [form="♀ (female)"]
  J21 = female alternating pin header, 1 pin [form="♀ (female)"]
  J18 = female pin header, 2 pins [form="♀ (female)"]

nets:
  N1: TO_SPEAKER.pin1, J21.pin1
  N2: TO_SPEAKER.pin2, J19.pin1, J18.pin2
  N3: J20.pin1, J18.pin1
