# Fritzing sketch GP2IO-0 (saved by Fritzing 0.9.2b)
circuit board: 7.1cm x 4.45cm
breadboards: 1

parts:
  ATMEGA328 = atmega328 [package=dip]
  3v = Voltage Regulator - 5V [package="TO220 [THT]"]  # not connected
  XTAL = Crystal [frequency="16 MHz" package=THT]
  PASSTHROUGH = IC, DIP package, 16 pins [chip_label=IC]
  C1 = Electrolytic Capacitor [capacitance=1µF package="100 mil [THT, electrolytic]"]
  D1 = Rectifier Diode [part_number=1N4001 package="300 mil [THT]"]
  D2 = Rectifier Diode [part_number=1N4001 package="300 mil [THT]"]
  270Ω = Resistor [tolerance=±5% resistance=270 package=THT]
  270Ω_2 = Resistor [tolerance=±5% resistance=270 package=THT]
  GAME_PORT = IC, DIP package, 16 pins [chip_label=IC]  # not connected

nets:
  N1: ATMEGA328.VCC, C1.+
  N2: ATMEGA328.XLAT1, XTAL.pin_1
  N3: ATMEGA328.XLAT2, XTAL.pin_0
  N4: ATMEGA328.A4, D2.anode
  N5: ATMEGA328.A5, D1.anode
  N6: PASSTHROUGH.pin2, D2.cathode, 270Ω.Pin_0
  N7: PASSTHROUGH.pin3, D1.cathode, 270Ω_2.Pin_0
  N8: PASSTHROUGH.pin8, C1.-
  N9: 270Ω.Pin_1, 270Ω_2.Pin_1

notes:
  5v
  GND
