# Fritzing sketch joystick-port-adapter-rotated (saved by Fritzing 0.9.2b)
circuit board: 3.17803cm x 3.17004cm
breadboards: 1

parts:
  X1 = DB9 Connector [package=db9]
  GAME = IC, DIP package, 16 pins [chip_label=IC]

nets:
  N1: X1.1, GAME.pin3
  N2: X1.2, GAME.pin1
  N3: X1.3, GAME.pin8
  N4: X1.5, GAME.pin6
  N5: X1.7, GAME.pin2
  N6: X1.8, GAME.pin10

notes:
  1
  9
  RetroConnector
  rev.2
  Game Port Adapter
