# Fritzing sketch retro-connector-IIc-PCB (saved by Fritzing 0.7.12b)
breadboards: 1

parts:
  J1 = shrouded pin header, 34 pins [form="♂ (shrouded male)"]
  Teensy++ = Teensy++ 2.0

nets:
  N1: J1.pin1, Teensy++.D3
  N2: J1.pin2, Teensy++.D2
  N3: J1.pin3, Teensy++.D1
  N4: J1.pin4, Teensy++.D0
  N5: J1.pin5, Teensy++.B7
  N6: J1.pin11, J1.pin12, J1.pin14, Teensy++.GND
  N7: J1.pin13, Teensy++.VCC
  N8: J1.pin16, Teensy++.B6
  N9: J1.pin17, Teensy++.B5
  N10: J1.pin18, Teensy++.B4
  N11: J1.pin19, Teensy++.B3
  N12: J1.pin21, Teensy++.B1
  N13: J1.pin22, Teensy++.F6
  N14: J1.pin23, Teensy++.D4
  N15: J1.pin24, Teensy++.D5
  N16: J1.pin25, Teensy++.F0
  N17: J1.pin26, Teensy++.D7
  N18: J1.pin27, Teensy++.F5
  N19: J1.pin28, Teensy++.C7
  N20: J1.pin29, Teensy++.C6
  N21: J1.pin30, Teensy++.C5
  N22: J1.pin31, Teensy++.C4
  N23: J1.pin32, Teensy++.C3
  N24: J1.pin33, Teensy++.C2
  N25: J1.pin34, Teensy++.C1

notes:
  RetroConnector
  Apple //c
  rev.2
  1
  34
  2

custom parts:
  Teensy++ 2.0: The Teensy is a complete USB-based microcontoller development system, in a very small footprint, capable of implementing many types of projects. All programming is done via the USB port. No special programmer is needed, only a standard "Mini-B" USB cable and a PC or Macintosh with a USB port.
