# Fritzing sketch retro-connector-IIc.pcb (saved by Fritzing 0.8.3b)
circuit board: 6.91115cm x 5.31912cm
breadboards: 1

parts:
  Teensy++ = IC, DIP package, 40 pins [chip_label=Teensy++]
  J2 = female pin header, 3 pins [form="♀ (female)"]
  J1 = shrouded pin header, 34 pins [form="♂ (shrouded male)"]
  J3 = female pin header, 3 pins [form="♀ (female)"]

nets:
  N1: Teensy++.pin2, J1.pin22
  N2: Teensy++.pin3, J1.pin27
  N3: Teensy++.pin8, J1.pin25
  N4: Teensy++.pin10, J1.pin11, J1.pin14
  N5: Teensy++.pin14, J1.pin21
  N6: Teensy++.pin16, J1.pin19
  N7: Teensy++.pin17, J1.pin18
  N8: Teensy++.pin18, J1.pin17
  N9: Teensy++.pin19, J1.pin16
  N10: Teensy++.pin20, J1.pin12, J1.pin13
  N11: Teensy++.pin22, J1.pin5
  N12: Teensy++.pin23, J1.pin4
  N13: Teensy++.pin24, J1.pin3
  N14: Teensy++.pin25, J1.pin2
  N15: Teensy++.pin26, J1.pin1
  N16: Teensy++.pin27, J1.pin23
  N17: Teensy++.pin28, J1.pin24
  N18: Teensy++.pin30, J1.pin26
  N19: Teensy++.pin31, J3.pin3
  N20: Teensy++.pin32, J3.pin2
  N21: Teensy++.pin33, J3.pin1
  N22: Teensy++.pin34, J1.pin34
  N23: Teensy++.pin35, J1.pin33
  N24: Teensy++.pin36, J1.pin32
  N25: Teensy++.pin37, J1.pin31
  N26: Teensy++.pin38, J1.pin30
  N27: Teensy++.pin39, J1.pin29
  N28: Teensy++.pin40, J1.pin28
  N29: J2.pin1, J1.pin10
  N30: J2.pin2, J1.pin8
  N31: J2.pin3, J1.pin6

notes:
  RetroConnector
  Apple //c
  rev.4
  1
  34
  2
  Keyboard Shield
  DISK LED
  KEYBOARD SW
  40/80 COL SW
  10  9  8
