# Fritzing sketch retro-connector-IIe-rev3-PCB (saved by Fritzing 0.8.0b)
breadboards: 1

parts:
  J1 = shrouded pin header, 26 pins [form="♂ (shrouded male)"]
  Teensy++ = Teensy++ 2.0

nets:
  N1: J1.pin1, Teensy++.C0
  N2: J1.pin2, Teensy++.VCC
  N3: J1.pin3, Teensy++.E1
  N4: J1.pin4, Teensy++.E0
  N5: J1.pin5, Teensy++.D7
  N6: J1.pin6, Teensy++.D5
  N7: J1.pin7, Teensy++.GND#0
  N8: J1.pin8, Teensy++.D4
  N9: J1.pin9, Teensy++.D3
  N10: J1.pin10, Teensy++.D2
  N11: J1.pin11, Teensy++.D1
  N12: J1.pin12, Teensy++.D0
  N13: J1.pin13, Teensy++.B7
  N14: J1.pin14, Teensy++.B2
  N15: J1.pin15, Teensy++.B1
  N16: J1.pin16, Teensy++.B0
  N17: J1.pin17, Teensy++.E7
  N18: J1.pin18, Teensy++.E6
  N19: J1.pin19, Teensy++.F0
  N20: J1.pin20, Teensy++.F1
  N21: J1.pin21, Teensy++.F2
  N22: J1.pin22, Teensy++.F3
  N23: J1.pin23, Teensy++.F4
  N24: J1.pin24, Teensy++.F5
  N25: J1.pin25, Teensy++.F6
  N26: J1.pin26, Teensy++.F7

notes:
  Apple //e
  2
  1
  26
  rev.3
  RetroConnector
