# Fritzing sketch retro-connector-rev2-PCB (saved by Fritzing 0.7.10b)
breadboards: 1

parts:
  Teensy++ = Teensy++ 2.0
  J1 = shrouded pin header, 26 pins [form="♂ (shrouded male)"]

nets:
  N1: Teensy++.GND#0, J1.pin7
  N2: Teensy++.B7, J1.pin13
  N3: Teensy++.D0, J1.pin12
  N4: Teensy++.D1, J1.pin11
  N5: Teensy++.D2, J1.pin10
  N6: Teensy++.D3, J1.pin9
  N7: Teensy++.D4, J1.pin8
  N8: Teensy++.D5, J1.pin6
  N9: Teensy++.D7, J1.pin5
  N10: Teensy++.E0, J1.pin4
  N11: Teensy++.E1, J1.pin3
  N12: Teensy++.C0, J1.pin1
  N13: Teensy++.F7, J1.pin26
  N14: Teensy++.F6, J1.pin25
  N15: Teensy++.F5, J1.pin24
  N16: Teensy++.F4, J1.pin23
  N17: Teensy++.F3, J1.pin22
  N18: Teensy++.F2, J1.pin21
  N19: Teensy++.F1, J1.pin20
  N20: Teensy++.F0, J1.pin19
  N21: Teensy++.E6, J1.pin18
  N22: Teensy++.E7, J1.pin17
  N23: Teensy++.B0, J1.pin16
  N24: Teensy++.B1, J1.pin15
  N25: Teensy++.B2, J1.pin14
  N26: Teensy++.VCC, J1.pin2

notes:
  RetroConnector
  Apple //e
  rev.2
  1
  26
  2
