# Fritzing sketch retro-connector-IIe-rev4.pcb (saved by Fritzing 0.8.3b)
circuit board: 6.61881cm x 4.309cm
breadboards: 1

parts:
  IC1 = IC, DIP package, 40 pins [chip_label=IC]
  J2 = shrouded pin header, 26 pins [form="♂ (shrouded male)"]

nets:
  N1: IC1.pin1, J2.pin7
  N2: IC1.pin2, J2.pin13
  N3: IC1.pin3, J2.pin12
  N4: IC1.pin4, J2.pin11
  N5: IC1.pin5, J2.pin10
  N6: IC1.pin6, J2.pin9
  N7: IC1.pin7, J2.pin8
  N8: IC1.pin8, J2.pin6
  N9: IC1.pin10, J2.pin5
  N10: IC1.pin11, J2.pin4
  N11: IC1.pin12, J2.pin3
  N12: IC1.pin13, J2.pin1
  N13: IC1.pin21, J2.pin26
  N14: IC1.pin22, J2.pin25
  N15: IC1.pin23, J2.pin24
  N16: IC1.pin24, J2.pin23
  N17: IC1.pin25, J2.pin22
  N18: IC1.pin26, J2.pin21
  N19: IC1.pin27, J2.pin20
  N20: IC1.pin28, J2.pin19
  N21: IC1.pin31, J2.pin18
  N22: IC1.pin32, J2.pin17
  N23: IC1.pin33, J2.pin16
  N24: IC1.pin34, J2.pin15
  N25: IC1.pin35, J2.pin14
  N26: IC1.pin40, J2.pin2

notes:
  Apple //e
  2
  1
  26
  rev.4
  RetroConnector
  Keyboard Shield
