# Fritzing sketch Joystick Shield PCB rev2 (saved by Fritzing 0.9.3b)
circuit board: 5.30607cm x 3.17758cm
breadboards: 1

parts:
  Game_Port = IC, DIP package, 16 pins [chip_label=IC]
  Teensy_2_0 = IC, DIP package, 24 pins [chip_label=IC]
  X1 = DB9 Connector [package=db9]
  100KΩ = Resistor [tolerance=±5% resistance=220 package=THT]
  100KΩ_2 = Resistor [tolerance=±5% resistance=220 package=THT]
  33KΩ = Resistor [tolerance=±5% resistance=220 package=THT]
  33KΩ_2 = Resistor [tolerance=±5% resistance=220 package=THT]
  ZERO = Pushbutton [package="[THT]"]

nets:
  N1: Game_Port.pin1, Teensy_2_0.pin24, X1.4
  N2: Game_Port.pin2, Teensy_2_0.pin11, X1.8, 33KΩ_2.Pin_1
  N3: Game_Port.pin3, Teensy_2_0.pin12, X1.5, 33KΩ.Pin_1
  N4: Game_Port.pin6, Teensy_2_0.pin15, X1.1, 100KΩ.Pin_1
  N5: Game_Port.pin8, Teensy_2_0.pin1, X1.3, 100KΩ.Pin_0, 100KΩ_2.Pin_0, 33KΩ.Pin_0, 33KΩ_2.Pin_0, ZERO.Pin_3, ZERO.Pin_4
  N6: Game_Port.pin10, Teensy_2_0.pin16, X1.7, 100KΩ_2.Pin_1
  N7: Teensy_2_0.pin2, ZERO.Pin_1, ZERO.Pin_2

notes:
  1
  9
  rev.2
  Joystick Shield
  RetroConnector
  Press ZERO button
  to recalibrate.
