# Fritzing sketch Joystick Shield PCB (saved by Fritzing 0.8.3b)
circuit board: 6.02541cm x 3.44311cm
breadboards: 1

parts:
  Game_Port = IC, DIP package, 16 pins [chip_label=IC]
  Teensy = IC, DIP package, 24 pins [chip_label=IC]
  X1 = DB9 Connector [package=db9]
  R1 = Resistor [tolerance=±5% resistance=220 package=THT]
  R2 = Resistor [tolerance=±5% resistance=220 package=THT]
  R3 = Resistor [tolerance=±5% resistance=220 package=THT]
  R4 = Resistor [tolerance=±5% resistance=220 package=THT]

nets:
  N1: Game_Port.pin1, Teensy.pin24, X1.4
  N2: Game_Port.pin2, Teensy.pin11, X1.8, R4.Pin_1
  N3: Game_Port.pin3, Teensy.pin12, X1.5, R3.Pin_1
  N4: Game_Port.pin6, Teensy.pin15, X1.1, R1.Pin_1
  N5: Game_Port.pin8, Teensy.pin1, X1.3, R1.Pin_0, R2.Pin_0, R3.Pin_0, R4.Pin_0
  N6: Game_Port.pin10, Teensy.pin16, X1.7, R2.Pin_1

notes:
  1
  16
  9
  rev.1
  Joystick
  RetroConnector
