# Fritzing sketch Joystick Shield (saved by Fritzing 0.8.3b)
circuit board: 6.02541cm x 3.44311cm
breadboards: 1

parts:
  Game_Port = IC, DIP package, 16 pins [chip_label=IC]
  Teensy = IC, DIP package, 24 pins [chip_label=IC]
  part = DB9 Connector [package=db9]

nets:
  N1: Game_Port.pin1, Teensy.pin24, part.4
  N2: Game_Port.pin2, Teensy.pin11, part.8
  N3: Game_Port.pin3, Teensy.pin12, part.5
  N4: Game_Port.pin6, Teensy.pin15, part.1
  N5: Game_Port.pin8, Teensy.pin1, part.3
  N6: Game_Port.pin10, Teensy.pin16, part.7

notes:
  1
  16
  9
  rev.1
  Joystick
  RetroConnector
