# Fritzing sketch M0100 USB (saved by Fritzing 0.9.0b)
circuit board: 3.17048cm x 3.9485cm
breadboards: 1

parts:
  1 = DB9 Connector [package=db9]
  Teensy_2_0 = IC, DIP package, 24 pins [chip_label=IC]

nets:
  N1: 1.1, 1.3, Teensy_2_0.pin1
  N2: 1.2, Teensy_2_0.pin24
  N3: 1.4, Teensy_2_0.pin7
  N4: 1.5, Teensy_2_0.pin8
  N5: 1.7, Teensy_2_0.pin6
  N6: 1.8, Teensy_2_0.pin9
  N7: 1.9, Teensy_2_0.pin10

notes:
  RetroConnector M0100
  rev.0
