# Fritzing sketch M0100-USB-V2-PCB (saved by Fritzing 0.9.2b)
circuit board: 3.17048cm x 4.45712cm
breadboards: 1

parts:
  1 = DB9 Connector [package=db9]
  Trinket_Pro_5V = Pro Trinket 5V
  TRIM = TRIMPOT [package=3362u-2]

nets:
  N1: 1.1, 1.3, Trinket_Pro_5V.GND
  N2: 1.2, Trinket_Pro_5V.VBUS, TRIM.CCW
  N3: 1.4, Trinket_Pro_5V.D9
  N4: 1.5, Trinket_Pro_5V.D10
  N5: 1.7, Trinket_Pro_5V.A3
  N6: 1.8, Trinket_Pro_5V.D5
  N7: 1.9, Trinket_Pro_5V.D4
  N8: Trinket_Pro_5V.A5, TRIM.WIPER

notes:
  RetroConnector M0100
  rev.2

custom parts:
  Pro Trinket 5V: The Pro Trinket 5V is like an Arduino Pro Mini with more pins and USB included. Built with the common core Arduino chip, the ATmega328p, it has 18 GPIO, 2 extra analog inputs, 28K of flash, and 2K of RAM. It has onboard USB bootloading support with Optiboot support, so you can either program your Pro Trinket over USB or with a FTDI cable. The Pro Trinket is programmable using the Arduino IDE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
