# Fritzing sketch serial-keyboard-IIe (saved by Fritzing 0.9.2b)
circuit board: 8.82732cm x 4.27805cm
breadboards: 1

parts:
  CTL+RESET = Pushbutton [package="[THT]"]
  R2 = Resistor [tolerance=±5% resistance=470 package=THT]
  R3 = Resistor [tolerance=±5% resistance=470 package=THT]
  S1 = Pushbutton [package="[THT]"]
  J18 = double row female pin header, 26 pins [form="♀ (female)"]
  J17 = double row female pin header, 26 pins [form="♀ (female)"]
  TEENSY_2_0 = IC, DIP package, 24 pins [chip_label=IC]
  CD4051B = IC, DIP package, 16 pins [chip_label=IC]
  CD74HC4067 = IC, DIP package, 24 pins [chip_label=CD74HC4067]

nets:
  N1: CTL+RESET.Pin_1, CTL+RESET.Pin_2, TEENSY_2_0.pin1, CD4051B.pin6, CD4051B.pin7, CD4051B.pin8
  N2: CTL+RESET.Pin_3, CTL+RESET.Pin_4, J18.pin8, J17.pin8, TEENSY_2_0.pin12
  N3: R2.Pin_0, S1.Pin_1, S1.Pin_2, J18.pin4, J17.pin4, TEENSY_2_0.pin11
  N4: R2.Pin_1, R3.Pin_1, J18.pin7, J17.pin7, CD74HC4067.pin12
  N5: R3.Pin_0, J18.pin3, J17.pin3
  N6: S1.Pin_3, S1.Pin_4, J18.pin2, J17.pin2, CD4051B.pin16, CD74HC4067.pin24
  N7: J18.pin1, J17.pin1, CD74HC4067.pin9
  N8: J18.pin5, J17.pin5
  N9: J18.pin6, J17.pin6
  N10: J18.pin9, J17.pin9, CD4051B.pin4
  N11: J18.pin10, J17.pin10, CD4051B.pin5
  N12: J18.pin11, J17.pin11, CD4051B.pin1
  N13: J18.pin12, J17.pin12, CD74HC4067.pin3
  N14: J18.pin13, J17.pin13, CD74HC4067.pin2
  N15: J18.pin14, J17.pin14, CD4051B.pin2
  N16: J18.pin15, J17.pin15, TEENSY_2_0.pin16
  N17: J18.pin16, J17.pin16, CD74HC4067.pin22
  N18: J18.pin17, J17.pin17, CD4051B.pin12
  N19: J18.pin18, J17.pin18, CD4051B.pin14
  N20: J18.pin19, J17.pin19, CD4051B.pin15
  N21: J18.pin20, J17.pin20, CD4051B.pin13
  N22: J18.pin21, J17.pin21, CD74HC4067.pin23
  N23: J18.pin22, J17.pin22, CD74HC4067.pin4
  N24: J18.pin23, J17.pin23, CD74HC4067.pin5
  N25: J18.pin24, J17.pin24, CD74HC4067.pin6
  N26: J18.pin25, J17.pin25, CD74HC4067.pin7
  N27: J18.pin26, J17.pin26, CD74HC4067.pin8
  N28: TEENSY_2_0.pin2, CD74HC4067.pin15
  N29: TEENSY_2_0.pin3, CD74HC4067.pin13
  N30: TEENSY_2_0.pin4, CD74HC4067.pin14
  N31: TEENSY_2_0.pin5, CD74HC4067.pin10
  N32: TEENSY_2_0.pin6, CD74HC4067.pin11
  N33: TEENSY_2_0.pin7, CD4051B.pin11
  N34: TEENSY_2_0.pin8, CD4051B.pin10
  N35: TEENSY_2_0.pin9, CD4051B.pin9
  N36: CD4051B.pin3, CD74HC4067.pin1

notes:
  rev.3
  Serial Keyboard Interface //e
  RetroConnector™
  ‹‹ PASSTHROUGH
  ‹‹ TO BOARD
  ‹‹ KEYBOARD
